// Logisim project cpu.circ as structural Verilog: 2 circuits, main circuit main
module main (
  input  [31:0] RS_READ_VALUE,
  input  [31:0] RT_READ_VALUE,
  input  [31:0] INSTRUCTION,
  input  CLOCK,
  input  RESET,
  output [31:0] t0,
  output [31:0] t1,
  output [31:0] t2,
  output [31:0] t3,
  output [4:0] RS,
  output [4:0] RT,
  output [4:0] Write_Register,
  output [31:0] RD_WRITE_VALUE,
  output RD_WRITE_ENABLE,
  output [23:0] FETCH_ADDRESS
);

  wire accessByte, ALU_signed_overflow, ALUEqual, beq, bne, branch, comparator_9_eq, comparator_10_eq,
       comparator_11_eq, ExtOp, j, jal, jr, jump, lui, MemtoReg, MemWr, MemWrite, nPC_sel, or_1_out,
       or_2_out, RegDst, RegWrite, use__t_star, zeroExtend;
  wire [1:0] aluSrc;
  wire [5:0] ALUCtr, aluOp, funct, opcode;
  wire [15:6] immediate;
  wire [23:0] adder_1_out, adder_2_out, bit_extender_1_out, bit_extender_2_out, bit_extender_3_out,
       bit_extender_4_out, checkbranch, checkjump, subtractor_1_out, subtractor_2_out;
  wire [25:16] jumpAddr;
  wire [31:0] alu_input_1, alu_input_2, aluOutput, bit_extender_5_out, bit_extender_6_out,
       bit_extender_7_out, bit_extender_8_out, dataMemIn, extended, FIXMEPLZ, MEM_data_mem_out,
       multiplexer_1_out, multiplexer_6_out, RegWr, shifter_1_out, shifter_2_out, t_read_1, t_read_2,
       writeNormal;

  Multiplexer #(.width(32), .enable("false")) multiplexer_1 (
    .in0(INSTRUCTION), .in1({32{1'b0}}), .out(multiplexer_1_out), .sel(or_1_out));
  or or_1 (or_1_out, branch, jal, jr, j);
  Bit_Extender #(.in_width(32), .out_width(24)) bit_extender_1 (.in(shifter_1_out), .out(bit_extender_1_out));
  Shifter #(.width(32), .shift("lr")) shifter_1 (.in(INSTRUCTION), .\dist (5'b00010), .out(shifter_1_out));
  Register #(.width(32)) register_1 (
    .D(multiplexer_1_out), .en(1'b1), .Q({opcode, jumpAddr, immediate, funct}), .clk(CLOCK));  // open: clr
  Adder #(.width(24)) adder_1 (.a(bit_extender_1_out), .b(24'h1), .out(adder_1_out));  // open: cin, cout
  assign bit_extender_2_out = {{8{immediate[15]}}, {immediate, funct}};  // Bit_Extender bit_extender_2
  Bit_Extender #(.in_width(26), .out_width(24)) bit_extender_3 (
    .in({jumpAddr, immediate, funct}), .out(bit_extender_3_out));
  Subtractor #(.width(24)) subtractor_1 (
    .a(bit_extender_3_out), .b(24'h100000), .out(subtractor_1_out));  // open: bin, bout
  Bit_Extender #(.in_width(32), .out_width(24)) bit_extender_4 (.in(INSTRUCTION), .out(bit_extender_4_out));
  Subtractor #(.width(24)) subtractor_2 (
    .a(bit_extender_4_out), .b(24'h100000), .out(subtractor_2_out));  // open: bin, bout
  Adder #(.width(24)) adder_2 (.a(adder_1_out), .b(bit_extender_2_out), .out(adder_2_out));  // open: cin, cout
  Multiplexer #(.width(24), .enable("false")) multiplexer_2 (
    .in0(checkbranch), .in1(subtractor_1_out), .out(checkjump), .sel(or_2_out));
  or or_2 (or_2_out, j, jal);
  Multiplexer #(.width(24), .enable("false")) multiplexer_3 (
    .in0(checkjump), .in1(subtractor_2_out), .out(FETCH_ADDRESS), .sel(jr));
  Multiplexer #(.width(24), .enable("false")) multiplexer_4 (
    .in0(adder_1_out), .in1(adder_2_out), .out(checkbranch), .sel(branch));
  control control (
    .INSTRUCTION(INSTRUCTION), .ALUEqual(ALUEqual), .nPC_sel(nPC_sel), .RegDst(RegDst), .RegWr(RegWr[0]),
    .ExtOp(ExtOp), .ALUSrc(aluSrc), .ALUCtr(ALUCtr), .MemWr(MemWr), .MemtoReg(MemtoReg), .Jump(jump),
    .AccessByte(accessByte));
  Comparator #(.width(6)) comparator_1 (.a(6'b000100), .b(opcode), .eq(beq));  // open: gt, lt
  Comparator #(.width(6)) comparator_2 (.a(6'b000101), .b(opcode), .eq(bne));  // open: gt, lt
  Comparator #(.width(6)) comparator_3 (.a(6'b000011), .b(opcode), .eq(jal));  // open: gt, lt
  Comparator #(.width(6)) comparator_4 (.a(6'b001000), .b(funct), .eq(jr));  // open: gt, lt
  Comparator #(.width(6)) comparator_5 (.a(6'b000010), .b(opcode), .eq(j));  // open: gt, lt
  Shifter #(.width(32)) shifter_2 (.in(extended), .\dist (5'b10000), .out(shifter_2_out));
  Multiplexer #(.width(32), .enable("false")) multiplexer_5 (
    .in0(writeNormal), .in1(shifter_2_out), .out(RegWr), .sel(lui));
  assign bit_extender_5_out = {{8{1'b0}}, FETCH_ADDRESS};  // Bit_Extender bit_extender_5
  Multiplexer #(.width(32), .enable("false")) multiplexer_6 (
    .in0(FIXMEPLZ), .in1(bit_extender_5_out), .out(multiplexer_6_out), .sel(jal));
  regfile_main RegFile (
    .Read_register_1(jumpAddr[22:21]), .Read_register_2(jumpAddr[17:16]), .write_register(immediate[12:11]),
    .write_data(multiplexer_6_out), .t0_Value(t0), .t1_Value(t1), .t2_Value(t2), .t3_Value(t3),
    .RegWrite(RegWrite), .clock(CLOCK), .Read_Data_1(t_read_1), .Read_Data_2(t_read_2));
  Comparator #(.width(3)) comparator_6 (.a(immediate[15:13]), .b(3'b010), .eq(use__t_star));  // open: gt, lt
  Comparator #(.width(3)) comparator_7 (.a(jumpAddr[20:18]), .b(3'b010), .eq(use__t_star));  // open: gt, lt
  Comparator #(.width(3)) comparator_8 (.a(jumpAddr[25:23]), .b(3'b010), .eq(use__t_star));  // open: gt, lt
  Multiplexer #(.width(32), .enable("false")) multiplexer_7 (
    .in0(RS_READ_VALUE), .in1(t_read_1), .out(alu_input_1), .sel(use__t_star));
  Multiplexer #(.width(32), .enable("false")) multiplexer_8 (
    .in0(RT_READ_VALUE), .in1(t_read_2), .out(alu_input_2), .sel(use__t_star));
  assign bit_extender_6_out = {{27{1'b0}}, immediate[10:6]};  // Bit_Extender bit_extender_6
  Comparator #(.width(6)) comparator_9 (.a(opcode), .b(6'b001100), .eq(comparator_9_eq));  // open: gt, lt
  Comparator #(.width(6)) comparator_10 (.a(opcode), .b(6'b001101), .eq(comparator_10_eq));  // open: gt, lt
  Comparator #(.width(6)) comparator_11 (.a(opcode), .b(6'b001111), .eq(comparator_11_eq));  // open: gt, lt
  assign bit_extender_7_out = {{16{immediate[15]}}, {immediate, funct}};  // Bit_Extender bit_extender_7
  assign bit_extender_8_out = {{16{1'b0}}, {immediate, funct}};  // Bit_Extender bit_extender_8
  Multiplexer #(.select(2), .width(32), .enable("false")) multiplexer_9 (
    .in0(RT_READ_VALUE), .in1(extended), .in2(bit_extender_6_out), .out(alu_input_2), .sel(aluSrc));  // open: in3
  or or_3 (zeroExtend, comparator_9_eq, comparator_10_eq, comparator_11_eq);
  Multiplexer #(.width(32), .enable("false")) multiplexer_10 (
    .in0(bit_extender_7_out), .in1(bit_extender_8_out), .out(extended), .sel(zeroExtend));
  alu_main ALU (
    .Switch__S(aluOp), .X(alu_input_1), .Equal(ALUEqual), .RESULT(aluOutput),
    .Signed_Overflow(ALU_signed_overflow), .Y(alu_input_2));
  LED led_1 (.in(ALU_signed_overflow));
  mem_main MEM (
    .Data_Mem_Addr(aluOutput), .Data_Mem_In(dataMemIn), .ACCESS_BYTE(accessByte), .MEM_WRITE(MemWrite),
    .CLOCK(CLOCK), .Data_Mem_Out(MEM_data_mem_out));
  Multiplexer #(.width(32), .enable("false")) multiplexer_11 (
    .in0(aluOutput), .in1(MEM_data_mem_out), .out(writeNormal), .sel(MemtoReg));
  // Pins of 1 and 32 bits meet at RegWr

  // Other names for the same wires on the sheet: fetchAddr[23:0] = FETCH_ADDRESS; immediate[5:0] = funct;
  //   jumpAddr[15:0] = {immediate, funct}; shamt[4:0] = immediate[10:6]; rd[4:0] = immediate[15:11];
  //   t__input__rd[1:0] = immediate[12:11]; rt_t[4:0] = jumpAddr[20:16]; t__input__rt[1:0] = jumpAddr[17:16];
  //   rs_t[4:0] = jumpAddr[25:21]; t__input__rs[1:0] = jumpAddr[22:21]; rdWriteEnable = RD_WRITE_ENABLE;
  //   rdWriteReg[31:0] = RD_WRITE_VALUE; rs_read[31:0] = RS_READ_VALUE; rt_read[31:0] = RT_READ_VALUE;
  //   writeRegister[4:0] = Write_Register

  // Notes on the sheet:
  //   These are outputs/inputs from run.circ
  //   These are outputs to run.circ
  //   Step 1: Instruction Fetch & PC Addressing
  //   Is bne supposed to be sign extended too?
  //   PC Addressing
  //   (To find extended, see Step 4)
  //   Fig 10: branch and jump instructions
  //   Step 2: decode into instruction types
  //   Fig 4: $t registers
  //   Step 3: Regfile for $t registers
  //   Fig 6: ALU src control
  //   Fig 7: immediate sign extension
  //   Step 4: Prepare for ALU
  //   Step 5: ALU
  //   Step 6: Memory
  //   Fig 3: memory
endmodule

module control (
  input  [31:0] INSTRUCTION,
  input  ALUEqual,
  input  nPC_sel,
  input  RegDst,
  input  RegWr,
  input  ExtOp,
  input  [1:0] ALUSrc,
  input  [5:0] ALUCtr,
  input  MemWr,
  input  MemtoReg,
  input  Jump,
  input  AccessByte
);

  wire addiu, and_1_out, and_2_out, and_3_out, andi, beq, bne, comparator_14_eq, comparator_15_eq,
       comparator_16_eq, comparator_17_eq, comparator_18_eq, comparator_19_eq, comparator_20_eq,
       comparator_21_eq, comparator_22_eq, comparator_23_eq, j, jal, jr, lb, lbu, lui, lw, not_1_out,
       not_2_out, or_1_out, or_2_out, or_3_out, or_4_out, or_5_out, or_6_out, or_7_out, or_8_out, or_9_out,
       or_10_out, ori;
  wire [5:0] funct, otherInstructions;

  Comparator #(.width(6)) comparator_1 (.a(6'b001001), .b(INSTRUCTION[31:26]), .eq(addiu));  // open: gt, lt
  Comparator #(.width(6)) comparator_2 (.a(6'b001100), .b(INSTRUCTION[31:26]), .eq(andi));  // open: gt, lt
  Comparator #(.width(6)) comparator_3 (.a(6'b001101), .b(INSTRUCTION[31:26]), .eq(ori));  // open: gt, lt
  Comparator #(.width(6)) comparator_4 (.a(INSTRUCTION[31:26]), .b(6'b001111), .eq(lui));  // open: gt, lt
  Comparator #(.width(6)) comparator_5 (.a(6'b100000), .b(INSTRUCTION[31:26]), .eq(lb));  // open: gt, lt
  Comparator #(.width(6)) comparator_6 (.a(6'b100100), .b(INSTRUCTION[31:26]), .eq(lbu));  // open: gt, lt
  Comparator #(.width(6)) comparator_7 (.a(6'b100011), .b(INSTRUCTION[31:26]), .eq(lw));  // open: gt, lt
  Comparator #(.width(6)) comparator_8 (.a(6'b101011), .b(INSTRUCTION[31:26]), .eq(MemWr));  // open: gt, lt
  Comparator #(.width(6)) comparator_9 (.a(6'b000100), .b(INSTRUCTION[31:26]), .eq(beq));  // open: gt, lt
  Comparator #(.width(6)) comparator_10 (.a(6'b000101), .b(INSTRUCTION[31:26]), .eq(bne));  // open: gt, lt
  Comparator #(.width(6)) comparator_11 (.a(6'b000011), .b(INSTRUCTION[31:26]), .eq(jal));  // open: gt, lt
  Comparator #(.width(6)) comparator_12 (.a(6'b001000), .b(INSTRUCTION[5:0]), .eq(jr));  // open: gt, lt
  Comparator #(.width(6)) comparator_13 (.a(6'b000010), .b(INSTRUCTION[31:26]), .eq(j));  // open: gt, lt
  Comparator #(.width(6)) comparator_14 (.a(INSTRUCTION[5:0]), .b(6'b000010), .eq(comparator_14_eq));  // open: gt, lt
  Comparator #(.width(6)) comparator_15 (.a(INSTRUCTION[5:0]), .b({6{1'b0}}), .eq(comparator_15_eq));  // open: gt, lt
  Comparator #(.width(6)) comparator_16 (.a(INSTRUCTION[5:0]), .b(6'b000011), .eq(comparator_16_eq));  // open: gt, lt
  Multiplexer multiplexer_1 (.in0(1'b0), .in1(1'b1), .out(RegDst), .sel(comparator_17_eq));  // open: en
  Comparator #(.width(6)) comparator_17 (.a(INSTRUCTION[31:26]), .b({6{1'b0}}), .eq(comparator_17_eq));  // open: gt, lt
  Comparator #(.width(6)) comparator_18 (.a(INSTRUCTION[31:26]), .b({6{1'b0}}), .eq(comparator_18_eq));  // open: gt, lt
  Multiplexer multiplexer_2 (.in0(1'b0), .in1(1'b1), .out(ExtOp), .sel(or_1_out));  // open: en
  or or_1 (or_1_out, addiu, lw, MemWr, lb, lbu);
  or or_2 (or_2_out, comparator_14_eq, comparator_15_eq, comparator_16_eq);
  or or_3 (or_3_out, addiu, andi, ori, lui, lb, lbu, lw, MemWr);
  or or_4 (or_4_out, addiu, andi, ori, lui, lb, lbu, lw, comparator_18_eq);
  Comparator #(.width(6)) comparator_19 (.a(INSTRUCTION[31:26]), .b({6{1'b0}}), .eq(comparator_19_eq));  // open: gt, lt
  not not_1 (not_1_out, or_2_out);
  assign ALUSrc = or_3_out ? 2'b01 : 2'bz;  // Controlled_Buffer imm
  Multiplexer multiplexer_3 (.in0(1'b0), .in1(1'b1), .out(RegWr), .sel(or_4_out));  // open: en
  assign ALUSrc = and_1_out ? 2'b00 : 2'bz;  // Controlled_Buffer reg
  and and_1 (and_1_out, comparator_19_eq, not_1_out);
  assign otherInstructions = andi ? 6'b100100 : 6'bz;  // Controlled_Buffer controlled_buffer_1
  assign otherInstructions = ori ? 6'b100101 : 6'bz;  // Controlled_Buffer controlled_buffer_2
  assign otherInstructions = lui ? {6{1'b0}} : 6'bz;  // Controlled_Buffer controlled_buffer_3
  Comparator #(.width(6)) comparator_20 (.a(INSTRUCTION[5:0]), .b(6'b000010), .eq(comparator_20_eq));  // open: gt, lt
  Comparator #(.width(6)) comparator_21 (.a(INSTRUCTION[5:0]), .b({6{1'b0}}), .eq(comparator_21_eq));  // open: gt, lt
  Comparator #(.width(6)) comparator_22 (.a(INSTRUCTION[5:0]), .b(6'b000011), .eq(comparator_22_eq));  // open: gt, lt
  assign otherInstructions = addiu ? 6'b100001 : 6'bz;  // Controlled_Buffer controlled_buffer_4
  assign otherInstructions = or_5_out ? 6'b100000 : 6'bz;  // Controlled_Buffer controlled_buffer_5
  or or_5 (or_5_out, lb, lw, MemWr, lbu);
  Multiplexer #(.width(6), .enable("false")) multiplexer_4 (
    .in0(otherInstructions), .in1(funct), .out(ALUCtr), .sel(comparator_23_eq));
  Comparator #(.width(6)) comparator_23 (.a(INSTRUCTION[31:26]), .b({6{1'b0}}), .eq(comparator_23_eq));  // open: gt, lt
  assign ALUSrc = or_6_out ? 2'b10 : 2'bz;  // Controlled_Buffer shamt
  or or_6 (or_6_out, comparator_20_eq, comparator_21_eq, comparator_22_eq);
  Multiplexer multiplexer_5 (.in0(1'b0), .in1(1'b1), .out(MemtoReg), .sel(or_7_out));  // open: en
  or or_7 (or_7_out, lb, lbu, lw);
  and and_2 (and_2_out, beq, ALUEqual);
  not not_2 (not_2_out, ALUEqual);
  and and_3 (and_3_out, not_2_out, bne);
  Multiplexer #(.enable("false")) multiplexer_6 (.in0(1'b0), .in1(1'b1), .out(AccessByte), .sel(or_8_out));
  or or_8 (or_8_out, lb, lbu);
  Multiplexer #(.enable("false")) multiplexer_7 (.in0(1'b0), .in1(1'b1), .out(Jump), .sel(or_9_out));
  or or_9 (or_9_out, j, jr, jal);
  or or_10 (or_10_out, and_2_out, and_3_out);
  Multiplexer multiplexer_8 (.in0(1'b0), .in1(1'b1), .out(nPC_sel), .sel(or_10_out));  // open: en

  // Other names for the same wires on the sheet: Fun[5:0] = INSTRUCTION[5:0]; Imm16[15:0] = INSTRUCTION[15:0];
  //   shamt[4:0] = INSTRUCTION[10:6]; Rd[4:0] = INSTRUCTION[15:11]; Rt[4:0] = INSTRUCTION[20:16];
  //   Rs[4:0] = INSTRUCTION[25:21]; Op[5:0] = INSTRUCTION[31:26]; sw = MemWr

  // Notes on the sheet:
  //   Inputs
  //   Outputs
endmodule
